// Logisim project Processor.circ as structural Verilog: 11 circuits, main circuit SR_FF
module SR_FF (
  input  in_1,
  input  in_2,
  input  in_3,
  output out_4,
  output out_5
);

  wire nand_1_out, nand_2_out;

  nand nand_1 (nand_1_out, in_1, in_2);
  nand nand_2 (nand_2_out, in_2, in_3);
  nand nand_3 (out_4, nand_1_out, out_5);
  nand nand_4 (out_5, out_4, nand_2_out);
endmodule

module Board (
  input  [3:0] in_1,
  input  [3:0] in_2,
  output out_3,
  output out_4,
  output out_5,
  output out_6,
  output out_7
);

  wire dipswitch_1_sw1, dipswitch_1_sw2, dipswitch_1_sw3;

  DipSwitch #(.number(3)) dipswitch_1 (.sw1(dipswitch_1_sw1), .sw2(dipswitch_1_sw2), .sw3(dipswitch_1_sw3));
  ALU alu_1 (
    .Acc(in_1), .D_Reg(in_2), .S0(dipswitch_1_sw3), .S1(dipswitch_1_sw2), .S2(dipswitch_1_sw1), .Ir(1'b0),
    .Il(1'b0), .Cout(out_5), .ResultToAcc({out_7, out_6, out_4, out_3}));
endmodule

module D_FF_level_triggered (
  input  in_1,
  input  CLK,
  output out_3,
  output out_4
);

  wire nand_1_out, nand_2_out, not_1_out;

  not not_1 (not_1_out, in_1);
  nand nand_1 (nand_1_out, in_1, CLK);
  nand nand_2 (nand_2_out, CLK, not_1_out);
  nand nand_3 (out_3, nand_1_out, out_4);
  nand nand_4 (out_4, out_3, nand_2_out);
endmodule

module PIPO_Register (
  input  in_1,
  input  in_2,
  input  in_3,
  input  in_4,
  input  LD,
  output out_6,
  output out_7,
  output out_8,
  output out_9
);

  wire d_ff_edge_triggered_1_out_4, d_ff_edge_triggered_2_out_4, d_ff_edge_triggered_3_out_4,
       d_ff_edge_triggered_4_out_4;

  D_FF_edge_triggered d_ff_edge_triggered_1 (
    .in_1(in_1), .in_2(LD), .out_3(out_6), .out_4(d_ff_edge_triggered_1_out_4));
  LED led_1 (.in(d_ff_edge_triggered_1_out_4));
  D_FF_edge_triggered d_ff_edge_triggered_2 (
    .in_1(in_2), .in_2(LD), .out_3(out_7), .out_4(d_ff_edge_triggered_2_out_4));
  LED led_2 (.in(d_ff_edge_triggered_2_out_4));
  D_FF_edge_triggered d_ff_edge_triggered_3 (
    .in_1(in_3), .in_2(LD), .out_3(out_8), .out_4(d_ff_edge_triggered_3_out_4));
  LED led_3 (.in(d_ff_edge_triggered_3_out_4));
  D_FF_edge_triggered d_ff_edge_triggered_4 (
    .in_1(in_4), .in_2(LD), .out_3(out_9), .out_4(d_ff_edge_triggered_4_out_4));
  LED led_4 (.in(d_ff_edge_triggered_4_out_4));
endmodule

module Accumulator (
  input  [3:0] in_1,
  input  LD,
  output [3:0] out_3
);

  PIPO_Register pipo_register_1 (
    .in_1(in_1[0]), .in_2(in_1[1]), .in_3(in_1[2]), .in_4(in_1[3]), .LD(LD), .out_6(out_3[0]),
    .out_7(out_3[1]), .out_8(out_3[2]), .out_9(out_3[3]));
endmodule

module Full_Adder (
  input  in_1,
  input  in_2,
  input  Cin,
  output Sum,
  output Cout
);

  wire and_1_out, and_2_out, xor_1_out;

  xor xor_1 (xor_1_out, in_1, in_2);
  and and_1 (and_1_out, xor_1_out, Cin);
  xor xor_2 (Sum, xor_1_out, Cin);
  and and_2 (and_2_out, in_2, in_1);
  or or_1 (Cout, and_1_out, and_2_out);
endmodule

module ALU (
  input  [3:0] Acc,
  input  [3:0] D_Reg,
  input  S0,
  input  S1,
  input  S2,
  input  Ir,
  input  Il,
  output Cout,
  output [3:0] ResultToAcc
);

  wire [3:0] and_1_out, fourbit_adder_subtractor_1_s0, not_1_out, or_1_out, shift_unit_1_s0, xor_1_out;

  assign not_1_out = ~Acc;  // NOT_Gate not_1, 4 bits wide
  assign and_1_out = Acc & D_Reg;  // AND_Gate and_1, 4 bits wide
  assign or_1_out = Acc | D_Reg;  // OR_Gate or_1, 4 bits wide
  assign xor_1_out = Acc ^ D_Reg;  // XOR_Gate xor_1, 4 bits wide
  FourBit_Adder_Subtractor fourbit_adder_subtractor_1 (
    .A0(Acc[0]), .A1(Acc[1]), .A2(Acc[2]), .A3(Acc[3]), .B0(D_Reg[0]), .B1(D_Reg[1]), .B2(D_Reg[2]),
    .B3(D_Reg[3]), .sub_mode(S0), .S0(fourbit_adder_subtractor_1_s0[0]),
    .S1(fourbit_adder_subtractor_1_s0[1]), .S2(fourbit_adder_subtractor_1_s0[2]),
    .S3(fourbit_adder_subtractor_1_s0[3]), .Cout(Cout));
  Shift_Unit shift_unit_1 (
    .Ir(Ir), .A0(Acc[0]), .A1(Acc[1]), .A2(Acc[2]), .A3(Acc[3]), .Il(Il), .right_shift(S0),
    .S0(shift_unit_1_s0[0]), .S1(shift_unit_1_s0[1]), .S2(shift_unit_1_s0[2]), .S3(shift_unit_1_s0[3]));
  Multiplexer #(.select(3), .width(4)) multiplexer_1 (
    .in0(fourbit_adder_subtractor_1_s0), .in1(fourbit_adder_subtractor_1_s0), .in2(not_1_out),
    .in3(and_1_out), .in4(or_1_out), .in5(xor_1_out), .in6(shift_unit_1_s0), .in7(shift_unit_1_s0),
    .out(ResultToAcc), .sel({S2, S1, S0}));
endmodule

module FourBit_Adder_Subtractor (
  input  A0,
  input  A1,
  input  A2,
  input  A3,
  input  B0,
  input  B1,
  input  B2,
  input  B3,
  input  sub_mode,
  output S0,
  output S1,
  output S2,
  output S3,
  output Cout
);

  wire full_adder_1_cout, full_adder_2_cout, full_adder_3_cout, xor_1_out, xor_2_out, xor_3_out, xor_4_out;

  xor xor_1 (xor_1_out, sub_mode, B0);
  xor xor_2 (xor_2_out, sub_mode, B1);
  xor xor_3 (xor_3_out, sub_mode, B2);
  xor xor_4 (xor_4_out, sub_mode, B3);
  Full_Adder full_adder_1 (.in_1(A0), .in_2(xor_1_out), .Cin(sub_mode), .Sum(S0), .Cout(full_adder_1_cout));
  Full_Adder full_adder_2 (.in_1(A1), .in_2(xor_2_out), .Cin(full_adder_1_cout), .Sum(S1), .Cout(full_adder_2_cout));
  Full_Adder full_adder_3 (.in_1(A2), .in_2(xor_3_out), .Cin(full_adder_2_cout), .Sum(S2), .Cout(full_adder_3_cout));
  Full_Adder full_adder_4 (.in_1(A3), .in_2(xor_4_out), .Cin(full_adder_3_cout), .Sum(S3), .Cout(Cout));
endmodule

module D_FF_edge_triggered (
  input  in_1,
  input  in_2,
  output out_3,
  output out_4
);

  D_Flip_Flop d_ff_1 (.D(in_1), .clk(in_2), .Q(out_3), .Qn(out_4));  // open: preset, reset
endmodule

module Shift_Unit (
  input  Ir,
  input  A0,
  input  A1,
  input  A2,
  input  A3,
  input  Il,
  input  right_shift,
  output S0,
  output S1,
  output S2,
  output S3
);

  Multiplexer multiplexer_1 (.in0(Ir), .in1(A1), .out(S0), .sel(right_shift));
  Multiplexer multiplexer_2 (.in0(A0), .in1(A2), .out(S1), .sel(right_shift));
  Multiplexer multiplexer_3 (.in0(A1), .in1(A3), .out(S2), .sel(right_shift));
  Multiplexer multiplexer_4 (.in0(A2), .in1(Il), .out(S3), .sel(right_shift));
endmodule

module SystemBus (
  input  [3:0] ADDBUS_L,
  input  [3:0] ADDBUS_H,
  input  in_3,
  input  in_4,
  input  in_5,
  input  in_6,
  input  in_7,
  input  T3,
  input  T2,
  input  T1,
  input  T0,
  output out_12,
  output [3:0] DataBus
);

  wire decoder_1_out0, decoder_1_out3, decoder_1_out5, decoder_1_out8, decoder_1_out9, decoder_1_out10,
       decoder_1_out11, decoder_1_out12, decoder_1_out13, decoder_1_out14, decoder_1_out15, decoder_2_out0,
       decoder_2_out1, decoder_2_out2, decoder_2_out3, not_1_out, or_1_out, or_2_out, or_3_out, or_4_out,
       or_5_out;
  wire [2:0] multiplexer_2_out;
  wire [3:0] ACC_out_3, alu_1_resulttoacc, BR_out_3, CR_out_3, DR_out_3, IR_out_3, multiplexer_1_out,
       ram_1_dout;

  Accumulator PC ();  // open: in_1, LD, out_3
  ALU alu_1 (
    .Acc(ACC_out_3), .D_Reg(DR_out_3), .S0(in_3), .S1(in_4), .S2(in_5), .Ir(1'b0), .Il(1'b0), .Cout(out_12),
    .ResultToAcc(alu_1_resulttoacc));
  Decoder #(.select(4)) decoder_1 (
    .out0(decoder_1_out0), .out3(decoder_1_out3), .out5(decoder_1_out5), .out8(decoder_1_out8),
    .out9(decoder_1_out9), .out10(decoder_1_out10), .out11(decoder_1_out11), .out12(decoder_1_out12),
    .out13(decoder_1_out13), .out14(decoder_1_out14), .out15(decoder_1_out15),
    .sel({in_6, in_5, in_4, in_3}), .en(in_7));  // open: out1, out2, out4, out6, out7
  Decoder #(.select(2)) decoder_2 (
    .out0(decoder_2_out0), .out1(decoder_2_out1), .out2(decoder_2_out2), .out3(decoder_2_out3),
    .sel(ADDBUS_L[1:0]), .en(decoder_1_out0));
  Hex_Digit_Display hex_digit_display_1 (.value(multiplexer_1_out));  // open: dp
  Multiplexer #(.width(4)) multiplexer_1 (
    .in0(alu_1_resulttoacc), .in1(DataBus), .out(multiplexer_1_out), .sel(decoder_1_out0));
  or or_1 (or_1_out, decoder_1_out11, decoder_1_out13);
  or or_2 (or_2_out, decoder_1_out3, decoder_1_out5, decoder_1_out8, decoder_1_out9, decoder_1_out10, decoder_1_out12, decoder_1_out14, decoder_1_out15);
  or or_3 (or_3_out, decoder_2_out2, decoder_1_out13);
  not not_1 (not_1_out, in_6);
  or or_4 (or_4_out, decoder_2_out3, or_2_out);
  RAM #(.dataWidth(4)) ram_1 (
    .addr({ADDBUS_H, ADDBUS_L}), .we(decoder_1_out11), .oe(or_5_out), .clk(or_1_out), .din(DataBus),
    .dout(ram_1_dout));
  or or_5 (or_5_out, decoder_1_out13, T0);
  Accumulator IR (.in_1(DataBus), .out_3(IR_out_3));  // open: LD
  Accumulator BR (.in_1(DataBus), .LD(decoder_2_out0), .out_3(BR_out_3));
  Accumulator CR (.in_1(DataBus), .LD(decoder_2_out1), .out_3(CR_out_3));
  Accumulator DR (.in_1(DataBus), .LD(or_3_out), .out_3(DR_out_3));
  Accumulator ACC (.in_1(multiplexer_1_out), .LD(or_4_out), .out_3(ACC_out_3));
  Hex_Digit_Display hex_digit_display_2 (.value(ACC_out_3));  // open: dp
  Hex_Digit_Display hex_digit_display_3 (.value(DR_out_3));  // open: dp
  Multiplexer #(.width(3)) multiplexer_2 (
    .in0({in_5, in_4, in_3}), .in1({1'b0, ADDBUS_L[3:2]}), .out(multiplexer_2_out), .sel(not_1_out));
  Hex_Digit_Display hex_digit_display_4 (.value(CR_out_3));  // open: dp
  Hex_Digit_Display hex_digit_display_5 (.value(BR_out_3));  // open: dp
  Multiplexer #(.select(3), .width(4)) multiplexer_3 (
    .in0(ACC_out_3), .in1(BR_out_3), .in2(CR_out_3), .in3(DR_out_3), .in4(IR_out_3), .in5(ram_1_dout),
    .out(DataBus), .sel(multiplexer_2_out));  // open: in6, in7
  Hex_Digit_Display hex_digit_display_6 (.value(DataBus));  // open: dp
endmodule
